// Logisim project cpu.circ as structural Verilog: 2 circuits, main circuit main
// reset
module main (
);

  wire adder_1_cout, adder_2_cout, alu_add, alu_cmp, alu_nand, alu_nor, alu_overflow, alu_sub, alu_swp,
       and_1_out, and_2_out, and_3_out, and_4_out, and_5_out, and_6_out, and_7_out, and_8_out, and_9_out,
       and_11_out, and_12_out, and_13_out, and_14_out, and_15_out, and_16_out, and_17_out, and_18_out,
       and_19_out, and_20_out, and_21_out, and_22_out, and_23_out, and_24_out, and_25_out, and_26_out,
       and_27_out, and_28_out, and_29_out, and_30_out, and_31_out, and_32_out, and_33_out, and_34_out,
       and_35_out, and_36_out, and_37_out, and_38_out, and_39_out, and_40_out, and_41_out, and_42_out,
       and_43_out, and_44_out, and_45_out, and_46_out, and_47_out, and_48_out, and_49_out, and_50_out,
       and_51_out, and_52_out, and_53_out, button_1_out, clock_1_out, cond_invert, d_ff_11_q,
       data_bus_to_reg_write_data, flags_write, imm16_to_reg2_read_data, imm16_to_reg_write_data, io_read,
       io_write, memory_write, microcode_stage1, microcode_stage2, nand_1_out, nand_2_out, nand_3_out,
       nand_4_out, nand_5_out, nand_6_out, nand_7_out, nand_8_out, nand_9_out, nand_10_out, nand_11_out,
       nand_12_out, nand_13_out, nand_14_out, nand_15_out, nand_16_out, nor_2_out, nor_3_out, nor_4_out,
       nor_5_out, nor_6_out, nor_7_out, nor_8_out, nor_9_out, nor_10_out, nor_11_out, nor_12_out, nor_13_out,
       nor_14_out, nor_15_out, nor_16_out, nor_17_out, not_1_out, not_2_out, not_3_out, not_4_out, not_5_out,
       not_6_out, not_7_out, not_8_out, not_9_out, not_10_out, not_11_out, not_12_out, not_13_out,
       not_14_out, not_15_out, not_16_out, not_17_out, not_18_out, not_19_out, not_20_out, not_21_out,
       not_22_out, not_23_out, not_24_out, not_25_out, not_26_out, not_27_out, not_28_out, not_29_out,
       not_30_out, not_31_out, not_32_out, not_33_out, not_34_out, not_35_out, not_36_out, not_37_out,
       not_38_out, not_39_out, not_40_out, not_41_out, not_42_out, not_43_out, not_44_out, not_45_out,
       not_46_out, not_47_out, not_48_out, not_49_out, not_50_out, not_51_out, not_52_out, not_53_out,
       not_54_out, not_55_out, not_56_out, not_57_out, not_58_out, not_59_out, not_60_out, or_1_out,
       or_2_out, or_3_out, or_4_out, or_5_out, or_6_out, or_7_out, pc_cound_cond_load_eq,
       pc_cound_cond_load_zero, pc_count, pc_count_load, pc_out_address_bus, reg1_read,
       reg1_to_reg_write_data, reg1_write, reg2_read, reg2_to_address_buss, reg2_to_reg_write_data,
       reg2_write, reset, switch_1_p2, transistor_317_out, transistor_318_out, transistor_319_out,
       transistor_320_out, transistor_321_out, transistor_322_out, transistor_323_out, transistor_324_out,
       transistor_325_out, transistor_326_out, transistor_327_out, transistor_328_out, transistor_329_out,
       transistor_330_out, transistor_331_out, transistor_332_out, transistor_381_out, transistor_382_out,
       transistor_383_out, transistor_384_out, transistor_385_out, transistor_386_out, transistor_387_out,
       transistor_388_out, transistor_389_out, transistor_390_out, transistor_391_out, transistor_392_out,
       transistor_393_out, transistor_394_out, transistor_395_out, transistor_396_out, xor_1_out, xor_2_out,
       xor_3_out, xor_4_out, xor_5_out, xor_6_out, xor_7_out, xor_8_out, xor_9_out, xor_10_out, xor_11_out,
       xor_12_out, xor_13_out, xor_14_out, xor_15_out, xor_16_out, xor_17_out, xor_18_out;
  wire [3:0] d_ff_1_q, instruction_reg1, instruction_reg2;
  wire [4:0] flags_in, flags_out;
  wire [7:0] data_bus, instruction, meory_bank, RAM_1_dout, register_2_q, register_3_q, register_4_q,
       register_5_q, register_6_q, register_7_q, register_8_q, register_9_q, register_10_q, register_11_q,
       register_12_q, rom_1_data, ROM_1_data_2, rom_2_data, rom_3_data;
  wire [15:0] adder_1_out, adder_2_out, address_bus, counter_1_q, instruction_imm16, io_port_0_in,
       io_port_0_out, reg1_read_data, reg2_read_data, reg_write_data;

  Button Button_1 (.out(reset));
  Clock clock_1 (.out(clock_1_out));
  // Switch switch_1: pin names not known; wires that end beside it: clock_1_out, switch_1_p2
  or or_1 (or_1_out, pc_count_load, pc_count);
  Pull_Resistor pull_resistor_1 (.node(switch_1_p2));
  Button button_1_dup2 (.out(button_1_out));
  ROM rom_1 (.addr(instruction), .data(rom_1_data));
  ROM rom_2 (.addr(instruction), .data(rom_2_data));
  ROM rom_3 (.addr(instruction), .data(rom_3_data));
  Counter #(.max('hffff), .width(16)) counter_1 (
    .clr(reset), .load(pc_count_load), .up(1'b1), .clk(or_1_out), .D(address_bus), .Q(counter_1_q));  // open: count, carry
  or or_2 (or_2_out, switch_1_p2, button_1_out);
  D_Flip_Flop d_ff_1 (.D(1'b1), .clk(or_2_out), .Q(d_ff_1_q[0]), .reset(or_3_out));  // open: Qn, preset
  ROM #(.addrWidth(15)) ROM_1_dup2 (.addr(address_bus[14:0]), .data(ROM_1_data_2));
  not not_1 (not_1_out, address_bus[14]);
  D_Flip_Flop d_ff_2 (.D(d_ff_1_q[0]), .clk(or_2_out), .Q(d_ff_1_q[1]), .reset(or_3_out));  // open: Qn, preset
  Register register_1 (.D(data_bus), .clk(d_ff_1_q[0]), .Q(instruction), .clr(or_3_out));  // open: en
  Pull_Resistor pull_resistor_2 (.node(instruction_reg1[0]));
  Pull_Resistor pull_resistor_3 (.node(instruction_reg1[1]));
  Pull_Resistor pull_resistor_4 (.node(instruction_reg1[2]));
  Pull_Resistor pull_resistor_5 (.node(instruction_reg1[3]));
  Pull_Resistor pull_resistor_6 (.node(instruction_reg2[0]));
  Pull_Resistor pull_resistor_7 (.node(instruction_reg2[1]));
  Pull_Resistor pull_resistor_8 (.node(instruction_reg2[2]));
  Pull_Resistor pull_resistor_9 (.node(instruction_reg2[3]));
  not not_2 (not_2_out, microcode_stage2);
  and and_1 (and_1_out, not_1_out, address_bus[15]);
  D_Flip_Flop d_ff_3 (.D(d_ff_1_q[1]), .clk(or_2_out), .Q(d_ff_1_q[2]), .reset(or_3_out));  // open: Qn, preset
  not not_3 (not_3_out, d_ff_1_q[3]);
  nor nor_1 (pc_out_address_bus, microcode_stage1, microcode_stage2);
  Register register_2 (.D(data_bus), .clk(d_ff_1_q[1]), .Q(register_2_q), .clr(or_3_out));  // open: en
  Transistor transistor_1 (.in(register_2_q[0]), .out(instruction_reg1[0]), .gate(not_10_out));
  Transistor transistor_2 (.in(register_2_q[1]), .out(instruction_reg1[1]), .gate(not_10_out));
  Transistor transistor_3 (.in(register_2_q[2]), .out(instruction_reg1[2]), .gate(not_10_out));
  Transistor transistor_4 (.in(register_2_q[3]), .out(instruction_reg1[3]), .gate(not_10_out));
  Transistor transistor_5 (.in(register_2_q[4]), .out(instruction_reg2[0]), .gate(not_10_out));
  Transistor transistor_6 (.in(register_2_q[5]), .out(instruction_reg2[1]), .gate(not_10_out));
  Transistor transistor_7 (.in(register_2_q[6]), .out(instruction_reg2[2]), .gate(not_10_out));
  Transistor transistor_8 (.in(register_2_q[7]), .out(instruction_reg2[3]), .gate(not_10_out));
  not not_4 (not_4_out, microcode_stage1);
  Pull_Resistor pull_resistor_10 (.node(reg1_read));
  Transistor transistor_9 (.in(rom_1_data[0]), .out(reg1_read), .gate(not_4_out));
  Pull_Resistor pull_resistor_11 (.node(reg2_read));
  Transistor transistor_10 (.in(rom_1_data[1]), .out(reg2_read), .gate(not_4_out));
  Pull_Resistor pull_resistor_12 (.node(reg1_to_reg_write_data));
  Transistor transistor_11 (.in(rom_1_data[2]), .out(reg1_to_reg_write_data), .gate(not_4_out));
  Pull_Resistor pull_resistor_13 (.node(reg2_to_reg_write_data));
  Transistor transistor_12 (.in(rom_1_data[3]), .out(reg2_to_reg_write_data), .gate(not_4_out));
  Pull_Resistor pull_resistor_14 (.node(data_bus_to_reg_write_data));
  Transistor transistor_13 (.in(rom_1_data[4]), .out(data_bus_to_reg_write_data), .gate(not_4_out));
  Pull_Resistor pull_resistor_15 (.node(imm16_to_reg_write_data));
  Transistor transistor_14 (.in(rom_1_data[5]), .out(imm16_to_reg_write_data), .gate(not_4_out));
  Pull_Resistor pull_resistor_16 (.node(alu_add));
  Transistor transistor_15 (.in(rom_1_data[6]), .out(alu_add), .gate(not_4_out));
  Pull_Resistor pull_resistor_17 (.node(alu_sub));
  Transistor transistor_16 (.in(rom_1_data[7]), .out(alu_sub), .gate(not_4_out));
  Pull_Resistor pull_resistor_18 (.node(alu_nor));
  Transistor transistor_17 (.in(rom_2_data[0]), .out(alu_nor), .gate(not_4_out));
  Pull_Resistor pull_resistor_19 (.node(alu_nand));
  Transistor transistor_18 (.in(rom_2_data[1]), .out(alu_nand), .gate(not_4_out));
  Pull_Resistor pull_resistor_20 (.node(imm16_to_reg2_read_data));
  Transistor transistor_19 (.in(rom_2_data[2]), .out(imm16_to_reg2_read_data), .gate(not_4_out));
  Pull_Resistor pull_resistor_21 (.node(reg2_to_address_buss));
  Transistor transistor_20 (.in(rom_2_data[3]), .out(reg2_to_address_buss), .gate(not_4_out));
  Pull_Resistor pull_resistor_22 (.node(alu_cmp));
  Transistor transistor_21 (.in(rom_2_data[4]), .out(alu_cmp), .gate(not_4_out));
  Pull_Resistor pull_resistor_23 (.node(alu_swp));
  Transistor transistor_22 (.in(rom_2_data[5]), .out(alu_swp), .gate(not_4_out));
  Pull_Resistor pull_resistor_24 (.node(cond_invert));
  Transistor transistor_23 (.in(rom_2_data[6]), .out(cond_invert), .gate(not_4_out));
  Pull_Resistor pull_resistor_25 (.node(io_read));
  Transistor transistor_24 (.in(rom_2_data[7]), .out(io_read), .gate(not_4_out));
  Pull_Resistor pull_resistor_26 (.node(reg1_write));
  Transistor transistor_25 (.in(rom_3_data[0]), .out(reg1_write), .gate(not_2_out));
  Pull_Resistor pull_resistor_27 (.node(reg2_write));
  Transistor transistor_26 (.in(rom_3_data[1]), .out(reg2_write), .gate(not_2_out));
  Pull_Resistor pull_resistor_28 (.node(pc_count_load));
  Transistor transistor_27 (.in(rom_3_data[2]), .out(pc_count_load), .gate(not_2_out));
  Pull_Resistor pull_resistor_29 (.node(flags_write));
  Transistor transistor_28 (.in(rom_3_data[3]), .out(flags_write), .gate(not_2_out));
  Pull_Resistor pull_resistor_30 (.node(memory_write));
  Transistor transistor_29 (.in(rom_3_data[4]), .out(memory_write), .gate(not_2_out));
  Pull_Resistor pull_resistor_31 (.node(pc_cound_cond_load_zero));
  Transistor transistor_30 (.in(rom_3_data[5]), .out(pc_cound_cond_load_zero), .gate(not_2_out));
  Pull_Resistor pull_resistor_32 (.node(pc_cound_cond_load_eq));
  Transistor transistor_31 (.in(rom_3_data[6]), .out(pc_cound_cond_load_eq), .gate(not_2_out));
  Pull_Resistor pull_resistor_33 (.node(io_write));
  Transistor transistor_32 (.in(rom_3_data[7]), .out(io_write), .gate(not_2_out));
  not not_5 (not_5_out, reg2_read_data[0]);
  not not_6 (not_6_out, reg2_read_data[1]);
  not not_7 (not_7_out, reg2_read_data[2]);
  not not_8 (not_8_out, reg2_read_data[3]);
  D_Flip_Flop d_ff_4 (
    .D(reg_write_data[15]), .clk(and_12_out), .Q(io_port_0_out[15]), .reset(reset));  // open: Qn, preset
  and and_2 (and_2_out, reg2_read_data[0], reg2_read_data[1]);
  and and_3 (and_3_out, reg2_read_data[2], reg2_read_data[3]);
  and and_4 (and_4_out, memory_write, and_1_out);
  Transistor transistor_33 (.in(counter_1_q[0]), .out(address_bus[0]), .gate(not_9_out));
  Transistor transistor_34 (.in(counter_1_q[1]), .out(address_bus[1]), .gate(not_9_out));
  Transistor transistor_35 (.in(counter_1_q[2]), .out(address_bus[2]), .gate(not_9_out));
  Transistor transistor_36 (.in(counter_1_q[3]), .out(address_bus[3]), .gate(not_9_out));
  Transistor transistor_37 (.in(counter_1_q[4]), .out(address_bus[4]), .gate(not_9_out));
  Transistor transistor_38 (.in(counter_1_q[5]), .out(address_bus[5]), .gate(not_9_out));
  Transistor transistor_39 (.in(counter_1_q[6]), .out(address_bus[6]), .gate(not_9_out));
  Transistor transistor_40 (.in(counter_1_q[7]), .out(address_bus[7]), .gate(not_9_out));
  Transistor transistor_41 (.in(counter_1_q[8]), .out(address_bus[8]), .gate(not_9_out));
  Transistor transistor_42 (.in(counter_1_q[9]), .out(address_bus[9]), .gate(not_9_out));
  Transistor transistor_43 (.in(counter_1_q[10]), .out(address_bus[10]), .gate(not_9_out));
  Transistor transistor_44 (.in(counter_1_q[11]), .out(address_bus[11]), .gate(not_9_out));
  Transistor transistor_45 (.in(counter_1_q[12]), .out(address_bus[12]), .gate(not_9_out));
  Transistor transistor_46 (.in(counter_1_q[13]), .out(address_bus[13]), .gate(not_9_out));
  Transistor transistor_47 (.in(counter_1_q[14]), .out(address_bus[14]), .gate(not_9_out));
  Transistor transistor_48 (.in(counter_1_q[15]), .out(address_bus[15]), .gate(not_9_out));
  not not_9 (not_9_out, pc_out_address_bus);
  D_Flip_Flop d_ff_5 (.D(d_ff_1_q[2]), .clk(or_2_out), .Q(d_ff_1_q[3]), .reset(or_3_out));  // open: Qn, preset
  and and_5 (and_5_out, or_2_out, not_3_out);
  Pull_Resistor pull_resistor_34 (.node(instruction_imm16[0]));
  Pull_Resistor pull_resistor_35 (.node(instruction_imm16[1]));
  Pull_Resistor pull_resistor_36 (.node(instruction_imm16[2]));
  Pull_Resistor pull_resistor_37 (.node(instruction_imm16[3]));
  Pull_Resistor pull_resistor_38 (.node(instruction_imm16[4]));
  Pull_Resistor pull_resistor_39 (.node(instruction_imm16[5]));
  Pull_Resistor pull_resistor_40 (.node(instruction_imm16[6]));
  Pull_Resistor pull_resistor_41 (.node(instruction_imm16[7]));
  Pull_Resistor pull_resistor_42 (.node(instruction_imm16[8]));
  Pull_Resistor pull_resistor_43 (.node(instruction_imm16[9]));
  Pull_Resistor pull_resistor_44 (.node(instruction_imm16[10]));
  Pull_Resistor pull_resistor_45 (.node(instruction_imm16[11]));
  Pull_Resistor pull_resistor_46 (.node(instruction_imm16[12]));
  Pull_Resistor pull_resistor_47 (.node(instruction_imm16[13]));
  Pull_Resistor pull_resistor_48 (.node(instruction_imm16[14]));
  Pull_Resistor pull_resistor_49 (.node(instruction_imm16[15]));
  and and_6 (and_6_out, not_5_out, not_6_out);
  and and_7 (and_7_out, not_7_out, not_8_out);
  D_Flip_Flop d_ff_6 (
    .D(reg_write_data[14]), .clk(and_12_out), .Q(io_port_0_out[14]), .reset(reset));  // open: Qn, preset
  RAM #(.addrWidth(14), .trigger("high")) RAM_1 (
    .addr(address_bus[13:0]), .we(and_4_out), .oe(and_1_out), .din(reg1_read_data[7:0]), .dout(RAM_1_dout));
  Pull_Resistor pull_resistor_50 (.node(address_bus[0]));
  Pull_Resistor pull_resistor_51 (.node(address_bus[1]));
  Pull_Resistor pull_resistor_52 (.node(address_bus[2]));
  Pull_Resistor pull_resistor_53 (.node(address_bus[3]));
  Pull_Resistor pull_resistor_54 (.node(address_bus[4]));
  Pull_Resistor pull_resistor_55 (.node(address_bus[5]));
  Pull_Resistor pull_resistor_56 (.node(address_bus[6]));
  Pull_Resistor pull_resistor_57 (.node(address_bus[7]));
  Pull_Resistor pull_resistor_58 (.node(address_bus[8]));
  Pull_Resistor pull_resistor_59 (.node(address_bus[9]));
  Pull_Resistor pull_resistor_60 (.node(address_bus[10]));
  Pull_Resistor pull_resistor_61 (.node(address_bus[11]));
  Pull_Resistor pull_resistor_62 (.node(address_bus[12]));
  Pull_Resistor pull_resistor_63 (.node(address_bus[13]));
  Pull_Resistor pull_resistor_64 (.node(address_bus[14]));
  Pull_Resistor pull_resistor_65 (.node(address_bus[15]));
  D_Flip_Flop d_ff_7 (.D(d_ff_1_q[3]), .clk(or_2_out), .Q(microcode_stage1), .reset(or_3_out));  // open: Qn, preset
  Register register_3 (.D(data_bus), .clk(d_ff_1_q[2]), .Q(register_3_q), .clr(or_3_out));  // open: en
  Transistor transistor_49 (.in(register_3_q[0]), .out(instruction_imm16[0]), .gate(not_10_out));
  Transistor transistor_50 (.in(register_3_q[1]), .out(instruction_imm16[1]), .gate(not_10_out));
  Transistor transistor_51 (.in(register_3_q[2]), .out(instruction_imm16[2]), .gate(not_10_out));
  Transistor transistor_52 (.in(register_3_q[3]), .out(instruction_imm16[3]), .gate(not_10_out));
  Transistor transistor_53 (.in(register_3_q[4]), .out(instruction_imm16[4]), .gate(not_10_out));
  Transistor transistor_54 (.in(register_3_q[5]), .out(instruction_imm16[5]), .gate(not_10_out));
  Transistor transistor_55 (.in(register_3_q[6]), .out(instruction_imm16[6]), .gate(not_10_out));
  Transistor transistor_56 (.in(register_3_q[7]), .out(instruction_imm16[7]), .gate(not_10_out));
  Transistor transistor_57 (.in(register_4_q[0]), .out(instruction_imm16[8]), .gate(not_10_out));
  Transistor transistor_58 (.in(register_4_q[1]), .out(instruction_imm16[9]), .gate(not_10_out));
  Transistor transistor_59 (.in(register_4_q[2]), .out(instruction_imm16[10]), .gate(not_10_out));
  Transistor transistor_60 (.in(register_4_q[3]), .out(instruction_imm16[11]), .gate(not_10_out));
  Transistor transistor_61 (.in(register_4_q[4]), .out(instruction_imm16[12]), .gate(not_10_out));
  Transistor transistor_62 (.in(register_4_q[5]), .out(instruction_imm16[13]), .gate(not_10_out));
  Transistor transistor_63 (.in(register_4_q[6]), .out(instruction_imm16[14]), .gate(not_10_out));
  Transistor transistor_64 (.in(register_4_q[7]), .out(instruction_imm16[15]), .gate(not_10_out));
  and and_8 (and_8_out, and_6_out, and_7_out);
  D_Flip_Flop d_ff_8 (
    .D(reg_write_data[13]), .clk(and_12_out), .Q(io_port_0_out[13]), .reset(reset));  // open: Qn, preset
  and and_9 (and_9_out, and_2_out, and_3_out);
  D_Flip_Flop d_ff_9 (
    .D(microcode_stage1), .clk(or_2_out), .Q(microcode_stage2), .reset(or_3_out));  // open: Qn, preset
  and and_10 (pc_count, and_5_out, d_ff_1_q[0]);
  Register register_4 (.D(data_bus), .clk(d_ff_1_q[3]), .Q(register_4_q), .clr(or_3_out));  // open: en
  not not_10 (not_10_out, microcode_stage1);
  and and_11 (and_11_out, and_8_out, io_read);
  and and_12 (and_12_out, and_8_out, io_write);
  D_Flip_Flop d_ff_10 (
    .D(reg_write_data[12]), .clk(and_12_out), .Q(io_port_0_out[12]), .reset(reset));  // open: Qn, preset
  and and_13 (and_13_out, and_9_out, io_write);
  Transistor transistor_65 (.in(ROM_1_data_2[0]), .out(data_bus[0]), .gate(address_bus[15]));
  Transistor transistor_66 (.in(ROM_1_data_2[1]), .out(data_bus[1]), .gate(address_bus[15]));
  Transistor transistor_67 (.in(ROM_1_data_2[2]), .out(data_bus[2]), .gate(address_bus[15]));
  Transistor transistor_68 (.in(ROM_1_data_2[3]), .out(data_bus[3]), .gate(address_bus[15]));
  Transistor transistor_69 (.in(ROM_1_data_2[4]), .out(data_bus[4]), .gate(address_bus[15]));
  Transistor transistor_70 (.in(ROM_1_data_2[5]), .out(data_bus[5]), .gate(address_bus[15]));
  Transistor transistor_71 (.in(ROM_1_data_2[6]), .out(data_bus[6]), .gate(address_bus[15]));
  Transistor transistor_72 (.in(ROM_1_data_2[7]), .out(data_bus[7]), .gate(address_bus[15]));
  D_Flip_Flop d_ff_11 (.D(microcode_stage2), .clk(or_2_out), .Q(d_ff_11_q), .reset(or_3_out));  // open: Qn, preset
  D_Flip_Flop d_ff_12 (
    .D(reg_write_data[11]), .clk(and_12_out), .Q(io_port_0_out[11]), .reset(reset));  // open: Qn, preset
  Pull_Resistor pull_resistor_66 (.node(data_bus[0]));
  Pull_Resistor pull_resistor_67 (.node(data_bus[1]));
  Pull_Resistor pull_resistor_68 (.node(data_bus[2]));
  Pull_Resistor pull_resistor_69 (.node(data_bus[3]));
  Pull_Resistor pull_resistor_70 (.node(data_bus[4]));
  Pull_Resistor pull_resistor_71 (.node(data_bus[5]));
  Pull_Resistor pull_resistor_72 (.node(data_bus[6]));
  Pull_Resistor pull_resistor_73 (.node(data_bus[7]));
  or or_3 (or_3_out, d_ff_11_q, reset);
  D_Flip_Flop d_ff_13 (
    .D(reg_write_data[10]), .clk(and_12_out), .Q(io_port_0_out[10]), .reset(reset));  // open: Qn, preset
  Transistor transistor_73 (.in(RAM_1_dout[0]), .out(data_bus[0]), .gate(not_11_out));
  Transistor transistor_74 (.in(RAM_1_dout[1]), .out(data_bus[1]), .gate(not_11_out));
  Transistor transistor_75 (.in(RAM_1_dout[2]), .out(data_bus[2]), .gate(not_11_out));
  Transistor transistor_76 (.in(RAM_1_dout[3]), .out(data_bus[3]), .gate(not_11_out));
  Transistor transistor_77 (.in(RAM_1_dout[4]), .out(data_bus[4]), .gate(not_11_out));
  Transistor transistor_78 (.in(RAM_1_dout[5]), .out(data_bus[5]), .gate(not_11_out));
  Transistor transistor_79 (.in(RAM_1_dout[6]), .out(data_bus[6]), .gate(not_11_out));
  Transistor transistor_80 (.in(RAM_1_dout[7]), .out(data_bus[7]), .gate(not_11_out));
  not not_11 (not_11_out, and_1_out);
  D_Flip_Flop d_ff_14 (
    .D(reg_write_data[9]), .clk(and_12_out), .Q(io_port_0_out[9]), .reset(reset));  // open: Qn, preset
  Transistor transistor_81 (.in(instruction_imm16[0]), .out(reg_write_data[0]), .gate(not_12_out));
  Transistor transistor_82 (.in(instruction_imm16[1]), .out(reg_write_data[1]), .gate(not_12_out));
  Transistor transistor_83 (.in(instruction_imm16[2]), .out(reg_write_data[2]), .gate(not_12_out));
  Transistor transistor_84 (.in(instruction_imm16[3]), .out(reg_write_data[3]), .gate(not_12_out));
  Transistor transistor_85 (.in(instruction_imm16[4]), .out(reg_write_data[4]), .gate(not_12_out));
  Transistor transistor_86 (.in(instruction_imm16[5]), .out(reg_write_data[5]), .gate(not_12_out));
  Transistor transistor_87 (.in(instruction_imm16[6]), .out(reg_write_data[6]), .gate(not_12_out));
  Transistor transistor_88 (.in(instruction_imm16[7]), .out(reg_write_data[7]), .gate(not_12_out));
  Transistor transistor_89 (.in(instruction_imm16[8]), .out(reg_write_data[8]), .gate(not_12_out));
  Transistor transistor_90 (.in(instruction_imm16[9]), .out(reg_write_data[9]), .gate(not_12_out));
  Transistor transistor_91 (.in(instruction_imm16[10]), .out(reg_write_data[10]), .gate(not_12_out));
  Transistor transistor_92 (.in(instruction_imm16[11]), .out(reg_write_data[11]), .gate(not_12_out));
  Transistor transistor_93 (.in(instruction_imm16[12]), .out(reg_write_data[12]), .gate(not_12_out));
  Transistor transistor_94 (.in(instruction_imm16[13]), .out(reg_write_data[13]), .gate(not_12_out));
  Transistor transistor_95 (.in(instruction_imm16[14]), .out(reg_write_data[14]), .gate(not_12_out));
  Transistor transistor_96 (.in(instruction_imm16[15]), .out(reg_write_data[15]), .gate(not_12_out));
  not not_12 (not_12_out, imm16_to_reg_write_data);
  D_Flip_Flop d_ff_15 (
    .D(reg_write_data[8]), .clk(and_12_out), .Q(io_port_0_out[8]), .reset(reset));  // open: Qn, preset
  xor xor_1 (xor_1_out, cond_invert, flags_out[0]);
  xor xor_2 (xor_2_out, cond_invert, flags_out[2]);
  D_Flip_Flop d_ff_16 (
    .D(reg_write_data[7]), .clk(and_12_out), .Q(io_port_0_out[7]), .reset(reset));  // open: Qn, preset
  D_Flip_Flop d_ff_17 (.D(reg_write_data[7]), .clk(and_13_out), .Q(meory_bank[7]), .reset(reset));  // open: Qn, preset
  not not_13 (not_13_out, pc_cound_cond_load_zero);
  Transistor transistor_97 (.in(xor_1_out), .out(pc_count_load), .gate(not_13_out));
  not not_14 (not_14_out, pc_cound_cond_load_eq);
  Transistor transistor_98 (.in(xor_2_out), .out(pc_count_load), .gate(not_14_out));
  D_Flip_Flop d_ff_18 (
    .D(reg_write_data[6]), .clk(and_12_out), .Q(io_port_0_out[6]), .reset(reset));  // open: Qn, preset
  D_Flip_Flop d_ff_19 (.D(reg_write_data[6]), .clk(and_13_out), .Q(meory_bank[6]), .reset(reset));  // open: Qn, preset
  not not_15 (not_15_out, imm16_to_reg2_read_data);
  D_Flip_Flop d_ff_20 (
    .D(reg_write_data[5]), .clk(and_12_out), .Q(io_port_0_out[5]), .reset(reset));  // open: Qn, preset
  D_Flip_Flop d_ff_21 (.D(reg_write_data[5]), .clk(and_13_out), .Q(meory_bank[5]), .reset(reset));  // open: Qn, preset
  Transistor transistor_99 (.in(reg1_read_data[0]), .out(reg_write_data[0]), .gate(not_16_out));
  Transistor transistor_100 (.in(reg1_read_data[1]), .out(reg_write_data[1]), .gate(not_16_out));
  Transistor transistor_101 (.in(reg1_read_data[2]), .out(reg_write_data[2]), .gate(not_16_out));
  Transistor transistor_102 (.in(reg1_read_data[3]), .out(reg_write_data[3]), .gate(not_16_out));
  Transistor transistor_103 (.in(reg1_read_data[4]), .out(reg_write_data[4]), .gate(not_16_out));
  Transistor transistor_104 (.in(reg1_read_data[5]), .out(reg_write_data[5]), .gate(not_16_out));
  Transistor transistor_105 (.in(reg1_read_data[6]), .out(reg_write_data[6]), .gate(not_16_out));
  Transistor transistor_106 (.in(reg1_read_data[7]), .out(reg_write_data[7]), .gate(not_16_out));
  Transistor transistor_107 (.in(reg1_read_data[8]), .out(reg_write_data[8]), .gate(not_16_out));
  Transistor transistor_108 (.in(reg1_read_data[9]), .out(reg_write_data[9]), .gate(not_16_out));
  Transistor transistor_109 (.in(reg1_read_data[10]), .out(reg_write_data[10]), .gate(not_16_out));
  Transistor transistor_110 (.in(reg1_read_data[11]), .out(reg_write_data[11]), .gate(not_16_out));
  Transistor transistor_111 (.in(reg1_read_data[12]), .out(reg_write_data[12]), .gate(not_16_out));
  Transistor transistor_112 (.in(reg1_read_data[13]), .out(reg_write_data[13]), .gate(not_16_out));
  Transistor transistor_113 (.in(reg1_read_data[14]), .out(reg_write_data[14]), .gate(not_16_out));
  Transistor transistor_114 (.in(reg1_read_data[15]), .out(reg_write_data[15]), .gate(not_16_out));
  not not_16 (not_16_out, reg1_to_reg_write_data);
  Transistor transistor_115 (.in(instruction_imm16[0]), .out(reg2_read_data[0]), .gate(not_15_out));
  Transistor transistor_116 (.in(instruction_imm16[1]), .out(reg2_read_data[1]), .gate(not_15_out));
  Transistor transistor_117 (.in(instruction_imm16[2]), .out(reg2_read_data[2]), .gate(not_15_out));
  Transistor transistor_118 (.in(instruction_imm16[3]), .out(reg2_read_data[3]), .gate(not_15_out));
  Transistor transistor_119 (.in(instruction_imm16[4]), .out(reg2_read_data[4]), .gate(not_15_out));
  Transistor transistor_120 (.in(instruction_imm16[5]), .out(reg2_read_data[5]), .gate(not_15_out));
  Transistor transistor_121 (.in(instruction_imm16[6]), .out(reg2_read_data[6]), .gate(not_15_out));
  Transistor transistor_122 (.in(instruction_imm16[7]), .out(reg2_read_data[7]), .gate(not_15_out));
  Transistor transistor_123 (.in(instruction_imm16[8]), .out(reg2_read_data[8]), .gate(not_15_out));
  Transistor transistor_124 (.in(instruction_imm16[9]), .out(reg2_read_data[9]), .gate(not_15_out));
  Transistor transistor_125 (.in(instruction_imm16[10]), .out(reg2_read_data[10]), .gate(not_15_out));
  Transistor transistor_126 (.in(instruction_imm16[11]), .out(reg2_read_data[11]), .gate(not_15_out));
  Transistor transistor_127 (.in(instruction_imm16[12]), .out(reg2_read_data[12]), .gate(not_15_out));
  Transistor transistor_128 (.in(instruction_imm16[13]), .out(reg2_read_data[13]), .gate(not_15_out));
  Transistor transistor_129 (.in(instruction_imm16[14]), .out(reg2_read_data[14]), .gate(not_15_out));
  Transistor transistor_130 (.in(instruction_imm16[15]), .out(reg2_read_data[15]), .gate(not_15_out));
  D_Flip_Flop d_ff_22 (
    .D(reg_write_data[4]), .clk(and_12_out), .Q(io_port_0_out[4]), .reset(reset));  // open: Qn, preset
  D_Flip_Flop d_ff_23 (.D(reg_write_data[4]), .clk(and_13_out), .Q(meory_bank[4]), .reset(reset));  // open: Qn, preset
  D_Flip_Flop d_ff_24 (
    .D(reg_write_data[3]), .clk(and_12_out), .Q(io_port_0_out[3]), .reset(reset));  // open: Qn, preset
  D_Flip_Flop d_ff_25 (.D(reg_write_data[3]), .clk(and_13_out), .Q(meory_bank[3]), .reset(reset));  // open: Qn, preset
  D_Flip_Flop d_ff_26 (
    .D(reg_write_data[2]), .clk(and_12_out), .Q(io_port_0_out[2]), .reset(reset));  // open: Qn, preset
  D_Flip_Flop d_ff_27 (.D(reg_write_data[2]), .clk(and_13_out), .Q(meory_bank[2]), .reset(reset));  // open: Qn, preset
  not not_17 (not_17_out, reg2_to_reg_write_data);
  Transistor transistor_131 (.in(instruction_imm16[0]), .out(address_bus[0]), .gate(not_18_out));
  Transistor transistor_132 (.in(instruction_imm16[1]), .out(address_bus[1]), .gate(not_18_out));
  Transistor transistor_133 (.in(instruction_imm16[2]), .out(address_bus[2]), .gate(not_18_out));
  Transistor transistor_134 (.in(instruction_imm16[3]), .out(address_bus[3]), .gate(not_18_out));
  Transistor transistor_135 (.in(instruction_imm16[4]), .out(address_bus[4]), .gate(not_18_out));
  Transistor transistor_136 (.in(instruction_imm16[5]), .out(address_bus[5]), .gate(not_18_out));
  Transistor transistor_137 (.in(instruction_imm16[6]), .out(address_bus[6]), .gate(not_18_out));
  Transistor transistor_138 (.in(instruction_imm16[7]), .out(address_bus[7]), .gate(not_18_out));
  Transistor transistor_139 (.in(instruction_imm16[8]), .out(address_bus[8]), .gate(not_18_out));
  Transistor transistor_140 (.in(instruction_imm16[9]), .out(address_bus[9]), .gate(not_18_out));
  Transistor transistor_141 (.in(instruction_imm16[10]), .out(address_bus[10]), .gate(not_18_out));
  Transistor transistor_142 (.in(instruction_imm16[11]), .out(address_bus[11]), .gate(not_18_out));
  Transistor transistor_143 (.in(instruction_imm16[12]), .out(address_bus[12]), .gate(not_18_out));
  Transistor transistor_144 (.in(instruction_imm16[13]), .out(address_bus[13]), .gate(not_18_out));
  Transistor transistor_145 (.in(instruction_imm16[14]), .out(address_bus[14]), .gate(not_18_out));
  Transistor transistor_146 (.in(instruction_imm16[15]), .out(address_bus[15]), .gate(not_18_out));
  not not_18 (not_18_out, reg2_to_address_buss);
  D_Flip_Flop d_ff_28 (
    .D(reg_write_data[1]), .clk(and_12_out), .Q(io_port_0_out[1]), .reset(reset));  // open: Qn, preset
  D_Flip_Flop d_ff_29 (.D(reg_write_data[1]), .clk(and_13_out), .Q(meory_bank[1]), .reset(reset));  // open: Qn, preset
  Transistor transistor_147 (.in(reg2_read_data[0]), .out(reg_write_data[0]), .gate(not_17_out));
  Transistor transistor_148 (.in(reg2_read_data[1]), .out(reg_write_data[1]), .gate(not_17_out));
  Transistor transistor_149 (.in(reg2_read_data[2]), .out(reg_write_data[2]), .gate(not_17_out));
  Transistor transistor_150 (.in(reg2_read_data[3]), .out(reg_write_data[3]), .gate(not_17_out));
  Transistor transistor_151 (.in(reg2_read_data[4]), .out(reg_write_data[4]), .gate(not_17_out));
  Transistor transistor_152 (.in(reg2_read_data[5]), .out(reg_write_data[5]), .gate(not_17_out));
  Transistor transistor_153 (.in(reg2_read_data[6]), .out(reg_write_data[6]), .gate(not_17_out));
  Transistor transistor_154 (.in(reg2_read_data[7]), .out(reg_write_data[7]), .gate(not_17_out));
  Transistor transistor_155 (.in(reg2_read_data[8]), .out(reg_write_data[8]), .gate(not_17_out));
  Transistor transistor_156 (.in(reg2_read_data[9]), .out(reg_write_data[9]), .gate(not_17_out));
  Transistor transistor_157 (.in(reg2_read_data[10]), .out(reg_write_data[10]), .gate(not_17_out));
  Transistor transistor_158 (.in(reg2_read_data[11]), .out(reg_write_data[11]), .gate(not_17_out));
  Transistor transistor_159 (.in(reg2_read_data[12]), .out(reg_write_data[12]), .gate(not_17_out));
  Transistor transistor_160 (.in(reg2_read_data[13]), .out(reg_write_data[13]), .gate(not_17_out));
  Transistor transistor_161 (.in(reg2_read_data[14]), .out(reg_write_data[14]), .gate(not_17_out));
  Transistor transistor_162 (.in(reg2_read_data[15]), .out(reg_write_data[15]), .gate(not_17_out));
  D_Flip_Flop d_ff_30 (
    .D(reg_write_data[0]), .clk(and_12_out), .Q(io_port_0_out[0]), .reset(reset));  // open: Qn, preset
  D_Flip_Flop d_ff_31 (.D(reg_write_data[0]), .clk(and_13_out), .Q(meory_bank[0]), .reset(reset));  // open: Qn, preset
  Pull_Resistor pull_resistor_74 (.node(io_port_0_in[0]));
  Pull_Resistor pull_resistor_75 (.node(io_port_0_in[1]));
  Pull_Resistor pull_resistor_76 (.node(io_port_0_in[2]));
  Pull_Resistor pull_resistor_77 (.node(io_port_0_in[3]));
  Pull_Resistor pull_resistor_78 (.node(io_port_0_in[4]));
  Pull_Resistor pull_resistor_79 (.node(io_port_0_in[5]));
  Pull_Resistor pull_resistor_80 (.node(io_port_0_in[6]));
  Pull_Resistor pull_resistor_81 (.node(io_port_0_in[7]));
  Pull_Resistor pull_resistor_82 (.node(io_port_0_in[8]));
  Pull_Resistor pull_resistor_83 (.node(io_port_0_in[9]));
  Pull_Resistor pull_resistor_84 (.node(io_port_0_in[10]));
  Pull_Resistor pull_resistor_85 (.node(io_port_0_in[11]));
  Pull_Resistor pull_resistor_86 (.node(io_port_0_in[12]));
  Pull_Resistor pull_resistor_87 (.node(io_port_0_in[13]));
  Pull_Resistor pull_resistor_88 (.node(io_port_0_in[14]));
  Pull_Resistor pull_resistor_89 (.node(io_port_0_in[15]));
  not not_19 (not_19_out, and_11_out);
  not not_20 (not_20_out, instruction_reg1[0]);
  not not_21 (not_21_out, instruction_reg1[1]);
  not not_22 (not_22_out, instruction_reg1[2]);
  not not_23 (not_23_out, instruction_reg1[3]);
  not not_24 (not_24_out, instruction_reg2[0]);
  not not_25 (not_25_out, instruction_reg2[1]);
  not not_26 (not_26_out, instruction_reg2[2]);
  not not_27 (not_27_out, instruction_reg2[3]);
  not not_28 (not_28_out, instruction_reg1[1]);
  not not_29 (not_29_out, instruction_reg1[2]);
  not not_30 (not_30_out, instruction_reg1[3]);
  not not_31 (not_31_out, instruction_reg2[1]);
  not not_32 (not_32_out, instruction_reg2[2]);
  not not_33 (not_33_out, instruction_reg2[3]);
  not not_34 (not_34_out, instruction_reg1[0]);
  not not_35 (not_35_out, instruction_reg1[2]);
  not not_36 (not_36_out, instruction_reg1[3]);
  not not_37 (not_37_out, instruction_reg2[0]);
  not not_38 (not_38_out, instruction_reg2[2]);
  not not_39 (not_39_out, instruction_reg2[3]);
  Transistor transistor_163 (.in(data_bus[0]), .out(reg_write_data[0]), .gate(not_40_out));
  Transistor transistor_164 (.in(data_bus[1]), .out(reg_write_data[1]), .gate(not_40_out));
  Transistor transistor_165 (.in(data_bus[2]), .out(reg_write_data[2]), .gate(not_40_out));
  Transistor transistor_166 (.in(data_bus[3]), .out(reg_write_data[3]), .gate(not_40_out));
  Transistor transistor_167 (.in(data_bus[4]), .out(reg_write_data[4]), .gate(not_40_out));
  Transistor transistor_168 (.in(data_bus[5]), .out(reg_write_data[5]), .gate(not_40_out));
  Transistor transistor_169 (.in(data_bus[6]), .out(reg_write_data[6]), .gate(not_40_out));
  Transistor transistor_170 (.in(data_bus[7]), .out(reg_write_data[7]), .gate(not_40_out));
  not not_40 (not_40_out, data_bus_to_reg_write_data);
  Transistor transistor_171 (.in(io_port_0_in[0]), .out(reg_write_data[0]), .gate(not_19_out));
  Transistor transistor_172 (.in(io_port_0_in[1]), .out(reg_write_data[1]), .gate(not_19_out));
  Transistor transistor_173 (.in(io_port_0_in[2]), .out(reg_write_data[2]), .gate(not_19_out));
  Transistor transistor_174 (.in(io_port_0_in[3]), .out(reg_write_data[3]), .gate(not_19_out));
  Transistor transistor_175 (.in(io_port_0_in[4]), .out(reg_write_data[4]), .gate(not_19_out));
  Transistor transistor_176 (.in(io_port_0_in[5]), .out(reg_write_data[5]), .gate(not_19_out));
  Transistor transistor_177 (.in(io_port_0_in[6]), .out(reg_write_data[6]), .gate(not_19_out));
  Transistor transistor_178 (.in(io_port_0_in[7]), .out(reg_write_data[7]), .gate(not_19_out));
  Transistor transistor_179 (.in(io_port_0_in[8]), .out(reg_write_data[8]), .gate(not_19_out));
  Transistor transistor_180 (.in(io_port_0_in[9]), .out(reg_write_data[9]), .gate(not_19_out));
  Transistor transistor_181 (.in(io_port_0_in[10]), .out(reg_write_data[10]), .gate(not_19_out));
  Transistor transistor_182 (.in(io_port_0_in[11]), .out(reg_write_data[11]), .gate(not_19_out));
  Transistor transistor_183 (.in(io_port_0_in[12]), .out(reg_write_data[12]), .gate(not_19_out));
  Transistor transistor_184 (.in(io_port_0_in[13]), .out(reg_write_data[13]), .gate(not_19_out));
  Transistor transistor_185 (.in(io_port_0_in[14]), .out(reg_write_data[14]), .gate(not_19_out));
  Transistor transistor_186 (.in(io_port_0_in[15]), .out(reg_write_data[15]), .gate(not_19_out));
  and and_14 (and_14_out, not_20_out, not_21_out);
  and and_15 (and_15_out, not_22_out, not_23_out);
  and and_16 (and_16_out, not_24_out, not_25_out);
  and and_17 (and_17_out, not_26_out, not_27_out);
  and and_18 (and_18_out, instruction_reg1[0], not_28_out);
  and and_19 (and_19_out, not_29_out, not_30_out);
  and and_20 (and_20_out, instruction_reg2[0], not_31_out);
  and and_21 (and_21_out, not_32_out, not_33_out);
  and and_22 (and_22_out, not_34_out, instruction_reg1[1]);
  and and_23 (and_23_out, not_35_out, not_36_out);
  and and_24 (and_24_out, not_37_out, instruction_reg2[1]);
  and and_25 (and_25_out, not_38_out, not_39_out);
  Pull_Resistor pull_resistor_90 (.node(reg_write_data[0]));
  Pull_Resistor pull_resistor_91 (.node(reg_write_data[1]));
  Pull_Resistor pull_resistor_92 (.node(reg_write_data[2]));
  Pull_Resistor pull_resistor_93 (.node(reg_write_data[3]));
  Pull_Resistor pull_resistor_94 (.node(reg_write_data[4]));
  Pull_Resistor pull_resistor_95 (.node(reg_write_data[5]));
  Pull_Resistor pull_resistor_96 (.node(reg_write_data[6]));
  Pull_Resistor pull_resistor_97 (.node(reg_write_data[7]));
  Pull_Resistor pull_resistor_98 (.node(reg_write_data[8]));
  Pull_Resistor pull_resistor_99 (.node(reg_write_data[9]));
  Pull_Resistor pull_resistor_100 (.node(reg_write_data[10]));
  Pull_Resistor pull_resistor_101 (.node(reg_write_data[11]));
  Pull_Resistor pull_resistor_102 (.node(reg_write_data[12]));
  Pull_Resistor pull_resistor_103 (.node(reg_write_data[13]));
  Pull_Resistor pull_resistor_104 (.node(reg_write_data[14]));
  Pull_Resistor pull_resistor_105 (.node(reg_write_data[15]));
  and and_26 (and_26_out, and_14_out, and_15_out);
  and and_27 (and_27_out, and_16_out, and_17_out);
  and and_28 (and_28_out, and_18_out, and_19_out);
  and and_29 (and_29_out, and_20_out, and_21_out);
  and and_30 (and_30_out, and_22_out, and_23_out);
  and and_31 (and_31_out, and_24_out, and_25_out);
  and and_32 (and_32_out, and_26_out, reg1_read);
  and and_33 (and_33_out, and_26_out, reg1_write);
  and and_34 (and_34_out, and_27_out, reg2_read);
  and and_35 (and_35_out, and_27_out, reg2_write);
  and and_36 (and_36_out, and_28_out, reg1_read);
  not not_41 (not_41_out, and_36_out);
  and and_37 (and_37_out, and_28_out, reg1_write);
  and and_38 (and_38_out, and_29_out, reg2_read);
  and and_39 (and_39_out, and_29_out, reg2_write);
  and and_40 (and_40_out, and_30_out, reg1_read);
  not not_42 (not_42_out, and_40_out);
  and and_41 (and_41_out, and_30_out, reg1_write);
  not not_43 (not_43_out, and_42_out);
  and and_42 (and_42_out, and_31_out, reg2_read);
  and and_43 (and_43_out, and_31_out, reg2_write);
  not not_44 (not_44_out, and_32_out);
  or or_4 (or_4_out, and_33_out, and_35_out);
  not not_45 (not_45_out, and_34_out);
  or or_5 (or_5_out, and_37_out, and_39_out);
  not not_46 (not_46_out, and_38_out);
  Register register_5 (.D(reg_write_data[7:0]), .clk(or_5_out), .Q(register_5_q), .clr(reset));  // open: en
  or or_6 (or_6_out, and_41_out, and_43_out);
  Register register_6 (.D(reg_write_data[7:0]), .clk(or_6_out), .Q(register_6_q), .clr(reset));  // open: en
  Register register_7 (.D(reg_write_data[7:0]), .clk(or_4_out), .Q(register_7_q), .clr(reset));  // open: en
  Register register_8 (.D(reg_write_data[15:8]), .clk(or_6_out), .Q(register_8_q), .clr(reset));  // open: en
  Register register_9 (.D(reg_write_data[15:8]), .clk(or_4_out), .Q(register_9_q), .clr(reset));  // open: en
  Register register_10 (.D(reg_write_data[15:8]), .clk(or_5_out), .Q(register_10_q), .clr(reset));  // open: en
  Transistor transistor_187 (.in(register_6_q[0]), .out(reg1_read_data[0]), .gate(not_42_out));
  Transistor transistor_188 (.in(register_6_q[1]), .out(reg1_read_data[1]), .gate(not_42_out));
  Transistor transistor_189 (.in(register_6_q[2]), .out(reg1_read_data[2]), .gate(not_42_out));
  Transistor transistor_190 (.in(register_6_q[3]), .out(reg1_read_data[3]), .gate(not_42_out));
  Transistor transistor_191 (.in(register_6_q[4]), .out(reg1_read_data[4]), .gate(not_42_out));
  Transistor transistor_192 (.in(register_6_q[5]), .out(reg1_read_data[5]), .gate(not_42_out));
  Transistor transistor_193 (.in(register_6_q[6]), .out(reg1_read_data[6]), .gate(not_42_out));
  Transistor transistor_194 (.in(register_6_q[7]), .out(reg1_read_data[7]), .gate(not_42_out));
  Transistor transistor_195 (.in(register_8_q[0]), .out(reg1_read_data[8]), .gate(not_42_out));
  Transistor transistor_196 (.in(register_8_q[1]), .out(reg1_read_data[9]), .gate(not_42_out));
  Transistor transistor_197 (.in(register_8_q[2]), .out(reg1_read_data[10]), .gate(not_42_out));
  Transistor transistor_198 (.in(register_8_q[3]), .out(reg1_read_data[11]), .gate(not_42_out));
  Transistor transistor_199 (.in(register_8_q[4]), .out(reg1_read_data[12]), .gate(not_42_out));
  Transistor transistor_200 (.in(register_8_q[5]), .out(reg1_read_data[13]), .gate(not_42_out));
  Transistor transistor_201 (.in(register_8_q[6]), .out(reg1_read_data[14]), .gate(not_42_out));
  Transistor transistor_202 (.in(register_8_q[7]), .out(reg1_read_data[15]), .gate(not_42_out));
  Transistor transistor_203 (.in(register_7_q[0]), .out(reg1_read_data[0]), .gate(not_44_out));
  Transistor transistor_204 (.in(register_7_q[1]), .out(reg1_read_data[1]), .gate(not_44_out));
  Transistor transistor_205 (.in(register_7_q[2]), .out(reg1_read_data[2]), .gate(not_44_out));
  Transistor transistor_206 (.in(register_7_q[3]), .out(reg1_read_data[3]), .gate(not_44_out));
  Transistor transistor_207 (.in(register_7_q[4]), .out(reg1_read_data[4]), .gate(not_44_out));
  Transistor transistor_208 (.in(register_7_q[5]), .out(reg1_read_data[5]), .gate(not_44_out));
  Transistor transistor_209 (.in(register_7_q[6]), .out(reg1_read_data[6]), .gate(not_44_out));
  Transistor transistor_210 (.in(register_7_q[7]), .out(reg1_read_data[7]), .gate(not_44_out));
  Transistor transistor_211 (.in(register_9_q[0]), .out(reg1_read_data[8]), .gate(not_44_out));
  Transistor transistor_212 (.in(register_9_q[1]), .out(reg1_read_data[9]), .gate(not_44_out));
  Transistor transistor_213 (.in(register_9_q[2]), .out(reg1_read_data[10]), .gate(not_44_out));
  Transistor transistor_214 (.in(register_9_q[3]), .out(reg1_read_data[11]), .gate(not_44_out));
  Transistor transistor_215 (.in(register_9_q[4]), .out(reg1_read_data[12]), .gate(not_44_out));
  Transistor transistor_216 (.in(register_9_q[5]), .out(reg1_read_data[13]), .gate(not_44_out));
  Transistor transistor_217 (.in(register_9_q[6]), .out(reg1_read_data[14]), .gate(not_44_out));
  Transistor transistor_218 (.in(register_9_q[7]), .out(reg1_read_data[15]), .gate(not_44_out));
  Transistor transistor_219 (.in(register_5_q[0]), .out(reg1_read_data[0]), .gate(not_41_out));
  Transistor transistor_220 (.in(register_5_q[1]), .out(reg1_read_data[1]), .gate(not_41_out));
  Transistor transistor_221 (.in(register_5_q[2]), .out(reg1_read_data[2]), .gate(not_41_out));
  Transistor transistor_222 (.in(register_5_q[3]), .out(reg1_read_data[3]), .gate(not_41_out));
  Transistor transistor_223 (.in(register_5_q[4]), .out(reg1_read_data[4]), .gate(not_41_out));
  Transistor transistor_224 (.in(register_5_q[5]), .out(reg1_read_data[5]), .gate(not_41_out));
  Transistor transistor_225 (.in(register_5_q[6]), .out(reg1_read_data[6]), .gate(not_41_out));
  Transistor transistor_226 (.in(register_5_q[7]), .out(reg1_read_data[7]), .gate(not_41_out));
  Transistor transistor_227 (.in(register_10_q[0]), .out(reg1_read_data[8]), .gate(not_41_out));
  Transistor transistor_228 (.in(register_10_q[1]), .out(reg1_read_data[9]), .gate(not_41_out));
  Transistor transistor_229 (.in(register_10_q[2]), .out(reg1_read_data[10]), .gate(not_41_out));
  Transistor transistor_230 (.in(register_10_q[3]), .out(reg1_read_data[11]), .gate(not_41_out));
  Transistor transistor_231 (.in(register_10_q[4]), .out(reg1_read_data[12]), .gate(not_41_out));
  Transistor transistor_232 (.in(register_10_q[5]), .out(reg1_read_data[13]), .gate(not_41_out));
  Transistor transistor_233 (.in(register_10_q[6]), .out(reg1_read_data[14]), .gate(not_41_out));
  Transistor transistor_234 (.in(register_10_q[7]), .out(reg1_read_data[15]), .gate(not_41_out));
  Transistor transistor_235 (.in(register_7_q[0]), .out(reg2_read_data[0]), .gate(not_45_out));
  Transistor transistor_236 (.in(register_7_q[1]), .out(reg2_read_data[1]), .gate(not_45_out));
  Transistor transistor_237 (.in(register_7_q[2]), .out(reg2_read_data[2]), .gate(not_45_out));
  Transistor transistor_238 (.in(register_7_q[3]), .out(reg2_read_data[3]), .gate(not_45_out));
  Transistor transistor_239 (.in(register_7_q[4]), .out(reg2_read_data[4]), .gate(not_45_out));
  Transistor transistor_240 (.in(register_7_q[5]), .out(reg2_read_data[5]), .gate(not_45_out));
  Transistor transistor_241 (.in(register_7_q[6]), .out(reg2_read_data[6]), .gate(not_45_out));
  Transistor transistor_242 (.in(register_7_q[7]), .out(reg2_read_data[7]), .gate(not_45_out));
  Transistor transistor_243 (.in(register_9_q[0]), .out(reg2_read_data[8]), .gate(not_45_out));
  Transistor transistor_244 (.in(register_9_q[1]), .out(reg2_read_data[9]), .gate(not_45_out));
  Transistor transistor_245 (.in(register_9_q[2]), .out(reg2_read_data[10]), .gate(not_45_out));
  Transistor transistor_246 (.in(register_9_q[3]), .out(reg2_read_data[11]), .gate(not_45_out));
  Transistor transistor_247 (.in(register_9_q[4]), .out(reg2_read_data[12]), .gate(not_45_out));
  Transistor transistor_248 (.in(register_9_q[5]), .out(reg2_read_data[13]), .gate(not_45_out));
  Transistor transistor_249 (.in(register_9_q[6]), .out(reg2_read_data[14]), .gate(not_45_out));
  Transistor transistor_250 (.in(register_9_q[7]), .out(reg2_read_data[15]), .gate(not_45_out));
  Transistor transistor_251 (.in(register_5_q[0]), .out(reg2_read_data[0]), .gate(not_46_out));
  Transistor transistor_252 (.in(register_5_q[1]), .out(reg2_read_data[1]), .gate(not_46_out));
  Transistor transistor_253 (.in(register_5_q[2]), .out(reg2_read_data[2]), .gate(not_46_out));
  Transistor transistor_254 (.in(register_5_q[3]), .out(reg2_read_data[3]), .gate(not_46_out));
  Transistor transistor_255 (.in(register_5_q[4]), .out(reg2_read_data[4]), .gate(not_46_out));
  Transistor transistor_256 (.in(register_5_q[5]), .out(reg2_read_data[5]), .gate(not_46_out));
  Transistor transistor_257 (.in(register_5_q[6]), .out(reg2_read_data[6]), .gate(not_46_out));
  Transistor transistor_258 (.in(register_5_q[7]), .out(reg2_read_data[7]), .gate(not_46_out));
  Transistor transistor_259 (.in(register_10_q[0]), .out(reg2_read_data[8]), .gate(not_46_out));
  Transistor transistor_260 (.in(register_10_q[1]), .out(reg2_read_data[9]), .gate(not_46_out));
  Transistor transistor_261 (.in(register_10_q[2]), .out(reg2_read_data[10]), .gate(not_46_out));
  Transistor transistor_262 (.in(register_10_q[3]), .out(reg2_read_data[11]), .gate(not_46_out));
  Transistor transistor_263 (.in(register_10_q[4]), .out(reg2_read_data[12]), .gate(not_46_out));
  Transistor transistor_264 (.in(register_10_q[5]), .out(reg2_read_data[13]), .gate(not_46_out));
  Transistor transistor_265 (.in(register_10_q[6]), .out(reg2_read_data[14]), .gate(not_46_out));
  Transistor transistor_266 (.in(register_10_q[7]), .out(reg2_read_data[15]), .gate(not_46_out));
  Transistor transistor_267 (.in(register_6_q[0]), .out(reg2_read_data[0]), .gate(not_43_out));
  Transistor transistor_268 (.in(register_6_q[1]), .out(reg2_read_data[1]), .gate(not_43_out));
  Transistor transistor_269 (.in(register_6_q[2]), .out(reg2_read_data[2]), .gate(not_43_out));
  Transistor transistor_270 (.in(register_6_q[3]), .out(reg2_read_data[3]), .gate(not_43_out));
  Transistor transistor_271 (.in(register_6_q[4]), .out(reg2_read_data[4]), .gate(not_43_out));
  Transistor transistor_272 (.in(register_6_q[5]), .out(reg2_read_data[5]), .gate(not_43_out));
  Transistor transistor_273 (.in(register_6_q[6]), .out(reg2_read_data[6]), .gate(not_43_out));
  Transistor transistor_274 (.in(register_6_q[7]), .out(reg2_read_data[7]), .gate(not_43_out));
  Transistor transistor_275 (.in(register_8_q[0]), .out(reg2_read_data[8]), .gate(not_43_out));
  Transistor transistor_276 (.in(register_8_q[1]), .out(reg2_read_data[9]), .gate(not_43_out));
  Transistor transistor_277 (.in(register_8_q[2]), .out(reg2_read_data[10]), .gate(not_43_out));
  Transistor transistor_278 (.in(register_8_q[3]), .out(reg2_read_data[11]), .gate(not_43_out));
  Transistor transistor_279 (.in(register_8_q[4]), .out(reg2_read_data[12]), .gate(not_43_out));
  Transistor transistor_280 (.in(register_8_q[5]), .out(reg2_read_data[13]), .gate(not_43_out));
  Transistor transistor_281 (.in(register_8_q[6]), .out(reg2_read_data[14]), .gate(not_43_out));
  Transistor transistor_282 (.in(register_8_q[7]), .out(reg2_read_data[15]), .gate(not_43_out));
  not not_47 (not_47_out, instruction_reg1[0]);
  not not_48 (not_48_out, instruction_reg1[1]);
  not not_49 (not_49_out, instruction_reg2[0]);
  not not_50 (not_50_out, instruction_reg2[1]);
  Pull_Resistor pull_resistor_106 (.node(reg_write_data[0]));
  Pull_Resistor pull_resistor_107 (.node(reg_write_data[1]));
  Pull_Resistor pull_resistor_108 (.node(reg_write_data[2]));
  Pull_Resistor pull_resistor_109 (.node(reg_write_data[3]));
  Pull_Resistor pull_resistor_110 (.node(reg_write_data[4]));
  Pull_Resistor pull_resistor_111 (.node(reg_write_data[5]));
  Pull_Resistor pull_resistor_112 (.node(reg_write_data[6]));
  Pull_Resistor pull_resistor_113 (.node(reg_write_data[7]));
  Pull_Resistor pull_resistor_114 (.node(reg_write_data[8]));
  Pull_Resistor pull_resistor_115 (.node(reg_write_data[9]));
  Pull_Resistor pull_resistor_116 (.node(reg_write_data[10]));
  Pull_Resistor pull_resistor_117 (.node(reg_write_data[11]));
  Pull_Resistor pull_resistor_118 (.node(reg_write_data[12]));
  Pull_Resistor pull_resistor_119 (.node(reg_write_data[13]));
  Pull_Resistor pull_resistor_120 (.node(reg_write_data[14]));
  Pull_Resistor pull_resistor_121 (.node(reg_write_data[15]));
  Adder #(.width(16)) adder_1 (
    .a(reg1_read_data), .b(reg2_read_data), .out(adder_1_out), .cout(adder_1_cout));  // open: cin
  Pull_Resistor pull_resistor_122 (.node(alu_overflow));
  Transistor transistor_283 (.in(adder_1_cout), .out(alu_overflow), .gate(not_51_out));
  and and_44 (and_44_out, not_47_out, not_48_out);
  and and_45 (and_45_out, instruction_reg1[2], instruction_reg1[3]);
  and and_46 (and_46_out, not_49_out, not_50_out);
  and and_47 (and_47_out, instruction_reg2[2], instruction_reg2[3]);
  Transistor transistor_284 (.in(adder_1_out[0]), .out(reg_write_data[0]), .gate(not_51_out));
  Transistor transistor_285 (.in(adder_1_out[1]), .out(reg_write_data[1]), .gate(not_51_out));
  Transistor transistor_286 (.in(adder_1_out[2]), .out(reg_write_data[2]), .gate(not_51_out));
  Transistor transistor_287 (.in(adder_1_out[3]), .out(reg_write_data[3]), .gate(not_51_out));
  Transistor transistor_288 (.in(adder_1_out[4]), .out(reg_write_data[4]), .gate(not_51_out));
  Transistor transistor_289 (.in(adder_1_out[5]), .out(reg_write_data[5]), .gate(not_51_out));
  Transistor transistor_290 (.in(adder_1_out[6]), .out(reg_write_data[6]), .gate(not_51_out));
  Transistor transistor_291 (.in(adder_1_out[7]), .out(reg_write_data[7]), .gate(not_51_out));
  Transistor transistor_292 (.in(adder_1_out[8]), .out(reg_write_data[8]), .gate(not_51_out));
  Transistor transistor_293 (.in(adder_1_out[9]), .out(reg_write_data[9]), .gate(not_51_out));
  Transistor transistor_294 (.in(adder_1_out[10]), .out(reg_write_data[10]), .gate(not_51_out));
  Transistor transistor_295 (.in(adder_1_out[11]), .out(reg_write_data[11]), .gate(not_51_out));
  Transistor transistor_296 (.in(adder_1_out[12]), .out(reg_write_data[12]), .gate(not_51_out));
  Transistor transistor_297 (.in(adder_1_out[13]), .out(reg_write_data[13]), .gate(not_51_out));
  Transistor transistor_298 (.in(adder_1_out[14]), .out(reg_write_data[14]), .gate(not_51_out));
  Transistor transistor_299 (.in(adder_1_out[15]), .out(reg_write_data[15]), .gate(not_51_out));
  not not_51 (not_51_out, alu_add);
  D_Flip_Flop d_ff_32 (
    .D(flags_in[4]), .clk(flags_write), .Q(flags_out[4]), .preset(alu_overflow), .reset(reset));  // open: Qn
  and and_48 (and_48_out, and_44_out, and_45_out);
  and and_49 (and_49_out, and_46_out, and_47_out);
  D_Flip_Flop d_ff_33 (
    .D(flags_in[2]), .clk(flags_write), .Q(flags_out[2]), .Qn(flags_out[3]), .reset(reset));  // open: preset
  and and_50 (and_50_out, and_48_out, reg1_read);
  and and_51 (and_51_out, and_48_out, reg1_write);
  and and_52 (and_52_out, and_49_out, reg2_read);
  and and_53 (and_53_out, and_49_out, reg2_write);
  Pull_Resistor pull_resistor_123 (.node(alu_overflow));
  Transistor transistor_300 (.in(adder_2_cout), .out(alu_overflow), .gate(not_54_out));
  D_Flip_Flop d_ff_34 (
    .D(flags_in[0]), .clk(flags_write), .Q(flags_out[0]), .Qn(flags_out[1]), .reset(reset));  // open: preset
  Pull_Resistor pull_resistor_124 (.node(reg1_read_data[0]));
  Pull_Resistor pull_resistor_125 (.node(reg1_read_data[1]));
  Pull_Resistor pull_resistor_126 (.node(reg1_read_data[2]));
  Pull_Resistor pull_resistor_127 (.node(reg1_read_data[3]));
  Pull_Resistor pull_resistor_128 (.node(reg1_read_data[4]));
  Pull_Resistor pull_resistor_129 (.node(reg1_read_data[5]));
  Pull_Resistor pull_resistor_130 (.node(reg1_read_data[6]));
  Pull_Resistor pull_resistor_131 (.node(reg1_read_data[7]));
  Pull_Resistor pull_resistor_132 (.node(reg1_read_data[8]));
  Pull_Resistor pull_resistor_133 (.node(reg1_read_data[9]));
  Pull_Resistor pull_resistor_134 (.node(reg1_read_data[10]));
  Pull_Resistor pull_resistor_135 (.node(reg1_read_data[11]));
  Pull_Resistor pull_resistor_136 (.node(reg1_read_data[12]));
  Pull_Resistor pull_resistor_137 (.node(reg1_read_data[13]));
  Pull_Resistor pull_resistor_138 (.node(reg1_read_data[14]));
  Pull_Resistor pull_resistor_139 (.node(reg1_read_data[15]));
  Pull_Resistor pull_resistor_140 (.node(reg2_read_data[0]));
  Pull_Resistor pull_resistor_141 (.node(reg2_read_data[1]));
  Pull_Resistor pull_resistor_142 (.node(reg2_read_data[2]));
  Pull_Resistor pull_resistor_143 (.node(reg2_read_data[3]));
  Pull_Resistor pull_resistor_144 (.node(reg2_read_data[4]));
  Pull_Resistor pull_resistor_145 (.node(reg2_read_data[5]));
  Pull_Resistor pull_resistor_146 (.node(reg2_read_data[6]));
  Pull_Resistor pull_resistor_147 (.node(reg2_read_data[7]));
  Pull_Resistor pull_resistor_148 (.node(reg2_read_data[8]));
  Pull_Resistor pull_resistor_149 (.node(reg2_read_data[9]));
  Pull_Resistor pull_resistor_150 (.node(reg2_read_data[10]));
  Pull_Resistor pull_resistor_151 (.node(reg2_read_data[11]));
  Pull_Resistor pull_resistor_152 (.node(reg2_read_data[12]));
  Pull_Resistor pull_resistor_153 (.node(reg2_read_data[13]));
  Pull_Resistor pull_resistor_154 (.node(reg2_read_data[14]));
  Pull_Resistor pull_resistor_155 (.node(reg2_read_data[15]));
  not not_52 (not_52_out, and_50_out);
  or or_7 (or_7_out, and_51_out, and_53_out);
  not not_53 (not_53_out, and_52_out);
  Adder #(.width(16)) adder_2 (
    .a(reg1_read_data), .b(reg2_read_data), .out(adder_2_out), .cout(adder_2_cout));  // open: cin
  Register register_11 (.D(reg_write_data[7:0]), .clk(or_7_out), .Q(register_11_q), .clr(reset));  // open: en
  Transistor transistor_301 (.in(adder_2_out[0]), .out(reg_write_data[0]), .gate(not_54_out));
  Transistor transistor_302 (.in(adder_2_out[1]), .out(reg_write_data[1]), .gate(not_54_out));
  Transistor transistor_303 (.in(adder_2_out[2]), .out(reg_write_data[2]), .gate(not_54_out));
  Transistor transistor_304 (.in(adder_2_out[3]), .out(reg_write_data[3]), .gate(not_54_out));
  Transistor transistor_305 (.in(adder_2_out[4]), .out(reg_write_data[4]), .gate(not_54_out));
  Transistor transistor_306 (.in(adder_2_out[5]), .out(reg_write_data[5]), .gate(not_54_out));
  Transistor transistor_307 (.in(adder_2_out[6]), .out(reg_write_data[6]), .gate(not_54_out));
  Transistor transistor_308 (.in(adder_2_out[7]), .out(reg_write_data[7]), .gate(not_54_out));
  Transistor transistor_309 (.in(adder_2_out[8]), .out(reg_write_data[8]), .gate(not_54_out));
  Transistor transistor_310 (.in(adder_2_out[9]), .out(reg_write_data[9]), .gate(not_54_out));
  Transistor transistor_311 (.in(adder_2_out[10]), .out(reg_write_data[10]), .gate(not_54_out));
  Transistor transistor_312 (.in(adder_2_out[11]), .out(reg_write_data[11]), .gate(not_54_out));
  Transistor transistor_313 (.in(adder_2_out[12]), .out(reg_write_data[12]), .gate(not_54_out));
  Transistor transistor_314 (.in(adder_2_out[13]), .out(reg_write_data[13]), .gate(not_54_out));
  Transistor transistor_315 (.in(adder_2_out[14]), .out(reg_write_data[14]), .gate(not_54_out));
  Transistor transistor_316 (.in(adder_2_out[15]), .out(reg_write_data[15]), .gate(not_54_out));
  not not_54 (not_54_out, alu_sub);
  Register register_12 (.D(reg_write_data[15:8]), .clk(or_7_out), .Q(register_12_q), .clr(reset));  // open: en
  xor xor_3 (xor_3_out, reg1_read_data[0], reg2_read_data[0]);
  xor xor_4 (xor_4_out, reg1_read_data[1], reg2_read_data[1]);
  xor xor_5 (xor_5_out, reg1_read_data[2], reg2_read_data[2]);
  xor xor_6 (xor_6_out, reg1_read_data[3], reg2_read_data[3]);
  xor xor_7 (xor_7_out, reg1_read_data[4], reg2_read_data[4]);
  xor xor_8 (xor_8_out, reg1_read_data[5], reg2_read_data[5]);
  xor xor_9 (xor_9_out, reg1_read_data[6], reg2_read_data[6]);
  xor xor_10 (xor_10_out, reg1_read_data[7], reg2_read_data[7]);
  xor xor_11 (xor_11_out, reg1_read_data[8], reg2_read_data[8]);
  xor xor_12 (xor_12_out, reg1_read_data[9], reg2_read_data[9]);
  xor xor_13 (xor_13_out, reg1_read_data[10], reg2_read_data[10]);
  xor xor_14 (xor_14_out, reg1_read_data[11], reg2_read_data[11]);
  xor xor_15 (xor_15_out, reg1_read_data[12], reg2_read_data[12]);
  xor xor_16 (xor_16_out, reg1_read_data[13], reg2_read_data[13]);
  xor xor_17 (xor_17_out, reg1_read_data[14], reg2_read_data[14]);
  xor xor_18 (xor_18_out, reg1_read_data[15], reg2_read_data[15]);
  Transistor transistor_317 (.in(1'b1), .out(transistor_317_out), .gate(xor_3_out));
  Transistor transistor_318 (.in(transistor_317_out), .out(transistor_318_out), .gate(xor_4_out));
  Transistor transistor_319 (.in(transistor_318_out), .out(transistor_319_out), .gate(xor_5_out));
  Transistor transistor_320 (.in(transistor_319_out), .out(transistor_320_out), .gate(xor_6_out));
  Transistor transistor_321 (.in(transistor_320_out), .out(transistor_321_out), .gate(xor_7_out));
  Transistor transistor_322 (.in(transistor_321_out), .out(transistor_322_out), .gate(xor_8_out));
  Transistor transistor_323 (.in(transistor_322_out), .out(transistor_323_out), .gate(xor_9_out));
  Transistor transistor_324 (.in(transistor_323_out), .out(transistor_324_out), .gate(xor_10_out));
  Transistor transistor_325 (.in(transistor_324_out), .out(transistor_325_out), .gate(xor_11_out));
  Transistor transistor_326 (.in(transistor_325_out), .out(transistor_326_out), .gate(xor_12_out));
  Transistor transistor_327 (.in(transistor_326_out), .out(transistor_327_out), .gate(xor_13_out));
  Transistor transistor_328 (.in(transistor_327_out), .out(transistor_328_out), .gate(xor_14_out));
  Transistor transistor_329 (.in(transistor_328_out), .out(transistor_329_out), .gate(xor_15_out));
  Transistor transistor_330 (.in(transistor_329_out), .out(transistor_330_out), .gate(xor_16_out));
  Transistor transistor_331 (.in(transistor_330_out), .out(transistor_331_out), .gate(xor_17_out));
  Transistor transistor_332 (.in(transistor_331_out), .out(transistor_332_out), .gate(xor_18_out));
  Pull_Resistor pull_resistor_156 (.node(transistor_332_out));
  Transistor transistor_333 (.in(register_11_q[0]), .out(reg1_read_data[0]), .gate(not_52_out));
  Transistor transistor_334 (.in(register_11_q[1]), .out(reg1_read_data[1]), .gate(not_52_out));
  Transistor transistor_335 (.in(register_11_q[2]), .out(reg1_read_data[2]), .gate(not_52_out));
  Transistor transistor_336 (.in(register_11_q[3]), .out(reg1_read_data[3]), .gate(not_52_out));
  Transistor transistor_337 (.in(register_11_q[4]), .out(reg1_read_data[4]), .gate(not_52_out));
  Transistor transistor_338 (.in(register_11_q[5]), .out(reg1_read_data[5]), .gate(not_52_out));
  Transistor transistor_339 (.in(register_11_q[6]), .out(reg1_read_data[6]), .gate(not_52_out));
  Transistor transistor_340 (.in(register_11_q[7]), .out(reg1_read_data[7]), .gate(not_52_out));
  Transistor transistor_341 (.in(register_12_q[0]), .out(reg1_read_data[8]), .gate(not_52_out));
  Transistor transistor_342 (.in(register_12_q[1]), .out(reg1_read_data[9]), .gate(not_52_out));
  Transistor transistor_343 (.in(register_12_q[2]), .out(reg1_read_data[10]), .gate(not_52_out));
  Transistor transistor_344 (.in(register_12_q[3]), .out(reg1_read_data[11]), .gate(not_52_out));
  Transistor transistor_345 (.in(register_12_q[4]), .out(reg1_read_data[12]), .gate(not_52_out));
  Transistor transistor_346 (.in(register_12_q[5]), .out(reg1_read_data[13]), .gate(not_52_out));
  Transistor transistor_347 (.in(register_12_q[6]), .out(reg1_read_data[14]), .gate(not_52_out));
  Transistor transistor_348 (.in(register_12_q[7]), .out(reg1_read_data[15]), .gate(not_52_out));
  Transistor transistor_349 (.in(register_11_q[0]), .out(reg2_read_data[0]), .gate(not_53_out));
  Transistor transistor_350 (.in(register_11_q[1]), .out(reg2_read_data[1]), .gate(not_53_out));
  Transistor transistor_351 (.in(register_11_q[2]), .out(reg2_read_data[2]), .gate(not_53_out));
  Transistor transistor_352 (.in(register_11_q[3]), .out(reg2_read_data[3]), .gate(not_53_out));
  Transistor transistor_353 (.in(register_11_q[4]), .out(reg2_read_data[4]), .gate(not_53_out));
  Transistor transistor_354 (.in(register_11_q[5]), .out(reg2_read_data[5]), .gate(not_53_out));
  Transistor transistor_355 (.in(register_11_q[6]), .out(reg2_read_data[6]), .gate(not_53_out));
  Transistor transistor_356 (.in(register_11_q[7]), .out(reg2_read_data[7]), .gate(not_53_out));
  Transistor transistor_357 (.in(register_12_q[0]), .out(reg2_read_data[8]), .gate(not_53_out));
  Transistor transistor_358 (.in(register_12_q[1]), .out(reg2_read_data[9]), .gate(not_53_out));
  Transistor transistor_359 (.in(register_12_q[2]), .out(reg2_read_data[10]), .gate(not_53_out));
  Transistor transistor_360 (.in(register_12_q[3]), .out(reg2_read_data[11]), .gate(not_53_out));
  Transistor transistor_361 (.in(register_12_q[4]), .out(reg2_read_data[12]), .gate(not_53_out));
  Transistor transistor_362 (.in(register_12_q[5]), .out(reg2_read_data[13]), .gate(not_53_out));
  Transistor transistor_363 (.in(register_12_q[6]), .out(reg2_read_data[14]), .gate(not_53_out));
  Transistor transistor_364 (.in(register_12_q[7]), .out(reg2_read_data[15]), .gate(not_53_out));
  Transistor transistor_365 (.in(nand_1_out), .out(reg_write_data[0]), .gate(not_55_out));
  nand nand_1 (nand_1_out, reg1_read_data[0], reg2_read_data[0]);
  Transistor transistor_366 (.in(nand_2_out), .out(reg_write_data[1]), .gate(not_55_out));
  nand nand_2 (nand_2_out, reg1_read_data[1], reg2_read_data[1]);
  Transistor transistor_367 (.in(nand_3_out), .out(reg_write_data[2]), .gate(not_55_out));
  nand nand_3 (nand_3_out, reg1_read_data[2], reg2_read_data[2]);
  Transistor transistor_368 (.in(nand_4_out), .out(reg_write_data[3]), .gate(not_55_out));
  nand nand_4 (nand_4_out, reg1_read_data[3], reg2_read_data[3]);
  Transistor transistor_369 (.in(nand_5_out), .out(reg_write_data[4]), .gate(not_55_out));
  nand nand_5 (nand_5_out, reg1_read_data[4], reg2_read_data[4]);
  Transistor transistor_370 (.in(nand_6_out), .out(reg_write_data[5]), .gate(not_55_out));
  nand nand_6 (nand_6_out, reg1_read_data[5], reg2_read_data[5]);
  Transistor transistor_371 (.in(nand_7_out), .out(reg_write_data[6]), .gate(not_55_out));
  nand nand_7 (nand_7_out, reg1_read_data[6], reg2_read_data[6]);
  Transistor transistor_372 (.in(nand_8_out), .out(reg_write_data[7]), .gate(not_55_out));
  nand nand_8 (nand_8_out, reg1_read_data[7], reg2_read_data[7]);
  Transistor transistor_373 (.in(nand_9_out), .out(reg_write_data[8]), .gate(not_55_out));
  nand nand_9 (nand_9_out, reg1_read_data[8], reg2_read_data[8]);
  Transistor transistor_374 (.in(nand_10_out), .out(reg_write_data[9]), .gate(not_55_out));
  nand nand_10 (nand_10_out, reg1_read_data[9], reg2_read_data[9]);
  Transistor transistor_375 (.in(nand_11_out), .out(reg_write_data[10]), .gate(not_55_out));
  nand nand_11 (nand_11_out, reg1_read_data[10], reg2_read_data[10]);
  Transistor transistor_376 (.in(nand_12_out), .out(reg_write_data[11]), .gate(not_55_out));
  nand nand_12 (nand_12_out, reg1_read_data[11], reg2_read_data[11]);
  Transistor transistor_377 (.in(nand_13_out), .out(reg_write_data[12]), .gate(not_55_out));
  nand nand_13 (nand_13_out, reg1_read_data[12], reg2_read_data[12]);
  Transistor transistor_378 (.in(nand_14_out), .out(reg_write_data[13]), .gate(not_55_out));
  nand nand_14 (nand_14_out, reg1_read_data[13], reg2_read_data[13]);
  Transistor transistor_379 (.in(nand_15_out), .out(reg_write_data[14]), .gate(not_55_out));
  nand nand_15 (nand_15_out, reg1_read_data[14], reg2_read_data[14]);
  Transistor transistor_380 (.in(nand_16_out), .out(reg_write_data[15]), .gate(not_55_out));
  nand nand_16 (nand_16_out, reg1_read_data[15], reg2_read_data[15]);
  not not_55 (not_55_out, alu_nand);
  Transistor transistor_381 (.in(1'b1), .out(transistor_381_out), .gate(reg1_read_data[0]));
  Transistor transistor_382 (.in(transistor_381_out), .out(transistor_382_out), .gate(reg1_read_data[1]));
  Transistor transistor_383 (.in(transistor_382_out), .out(transistor_383_out), .gate(reg1_read_data[2]));
  Transistor transistor_384 (.in(transistor_383_out), .out(transistor_384_out), .gate(reg1_read_data[3]));
  Transistor transistor_385 (.in(transistor_384_out), .out(transistor_385_out), .gate(reg1_read_data[4]));
  Transistor transistor_386 (.in(transistor_385_out), .out(transistor_386_out), .gate(reg1_read_data[5]));
  Transistor transistor_387 (.in(transistor_386_out), .out(transistor_387_out), .gate(reg1_read_data[6]));
  Transistor transistor_388 (.in(transistor_387_out), .out(transistor_388_out), .gate(reg1_read_data[7]));
  Transistor transistor_389 (.in(transistor_388_out), .out(transistor_389_out), .gate(reg1_read_data[8]));
  Transistor transistor_390 (.in(transistor_389_out), .out(transistor_390_out), .gate(reg1_read_data[9]));
  Transistor transistor_391 (.in(transistor_390_out), .out(transistor_391_out), .gate(reg1_read_data[10]));
  Transistor transistor_392 (.in(transistor_391_out), .out(transistor_392_out), .gate(reg1_read_data[11]));
  Transistor transistor_393 (.in(transistor_392_out), .out(transistor_393_out), .gate(reg1_read_data[12]));
  Transistor transistor_394 (.in(transistor_393_out), .out(transistor_394_out), .gate(reg1_read_data[13]));
  Transistor transistor_395 (.in(transistor_394_out), .out(transistor_395_out), .gate(reg1_read_data[14]));
  Transistor transistor_396 (.in(transistor_395_out), .out(transistor_396_out), .gate(reg1_read_data[15]));
  Pull_Resistor pull_resistor_157 (.node(transistor_396_out));
  nor nor_2 (nor_2_out, reg1_read_data[0], reg2_read_data[0]);
  nor nor_3 (nor_3_out, reg1_read_data[1], reg2_read_data[1]);
  nor nor_4 (nor_4_out, reg1_read_data[2], reg2_read_data[2]);
  nor nor_5 (nor_5_out, reg1_read_data[3], reg2_read_data[3]);
  nor nor_6 (nor_6_out, reg1_read_data[4], reg2_read_data[4]);
  nor nor_7 (nor_7_out, reg1_read_data[5], reg2_read_data[5]);
  nor nor_8 (nor_8_out, reg1_read_data[6], reg2_read_data[6]);
  nor nor_9 (nor_9_out, reg1_read_data[7], reg2_read_data[7]);
  nor nor_10 (nor_10_out, reg1_read_data[8], reg2_read_data[8]);
  nor nor_11 (nor_11_out, reg1_read_data[9], reg2_read_data[9]);
  nor nor_12 (nor_12_out, reg1_read_data[10], reg2_read_data[10]);
  nor nor_13 (nor_13_out, reg1_read_data[11], reg2_read_data[11]);
  nor nor_14 (nor_14_out, reg1_read_data[12], reg2_read_data[12]);
  nor nor_15 (nor_15_out, reg1_read_data[13], reg2_read_data[13]);
  nor nor_16 (nor_16_out, reg1_read_data[14], reg2_read_data[14]);
  nor nor_17 (nor_17_out, reg1_read_data[15], reg2_read_data[15]);
  not not_56 (not_56_out, alu_nor);
  not not_57 (not_57_out, alu_cmp);
  not not_58 (not_58_out, transistor_396_out);
  not not_59 (not_59_out, transistor_332_out);
  Transistor transistor_397 (.in(nor_2_out), .out(reg_write_data[0]), .gate(not_56_out));
  Transistor transistor_398 (.in(nor_3_out), .out(reg_write_data[1]), .gate(not_56_out));
  Transistor transistor_399 (.in(nor_4_out), .out(reg_write_data[2]), .gate(not_56_out));
  Transistor transistor_400 (.in(nor_5_out), .out(reg_write_data[3]), .gate(not_56_out));
  Transistor transistor_401 (.in(nor_6_out), .out(reg_write_data[4]), .gate(not_56_out));
  Transistor transistor_402 (.in(nor_7_out), .out(reg_write_data[5]), .gate(not_56_out));
  Transistor transistor_403 (.in(nor_8_out), .out(reg_write_data[6]), .gate(not_56_out));
  Transistor transistor_404 (.in(nor_9_out), .out(reg_write_data[7]), .gate(not_56_out));
  Transistor transistor_405 (.in(nor_10_out), .out(reg_write_data[8]), .gate(not_56_out));
  Transistor transistor_406 (.in(nor_11_out), .out(reg_write_data[9]), .gate(not_56_out));
  Transistor transistor_407 (.in(nor_12_out), .out(reg_write_data[10]), .gate(not_56_out));
  Transistor transistor_408 (.in(nor_13_out), .out(reg_write_data[11]), .gate(not_56_out));
  Transistor transistor_409 (.in(nor_14_out), .out(reg_write_data[12]), .gate(not_56_out));
  Transistor transistor_410 (.in(nor_15_out), .out(reg_write_data[13]), .gate(not_56_out));
  Transistor transistor_411 (.in(nor_16_out), .out(reg_write_data[14]), .gate(not_56_out));
  Transistor transistor_412 (.in(nor_17_out), .out(reg_write_data[15]), .gate(not_56_out));
  Transistor transistor_413 (.in(transistor_396_out), .out(flags_in[0]), .gate(not_57_out));
  Transistor transistor_414 (.in(not_58_out), .out(flags_in[1]), .gate(not_57_out));
  Transistor transistor_415 (.in(transistor_332_out), .out(flags_in[2]), .gate(not_57_out));
  Transistor transistor_416 (.in(not_59_out), .out(flags_in[3]), .gate(not_57_out));
  Pull_Resistor pull_resistor_158 (.node(flags_in[0]));
  Pull_Resistor pull_resistor_159 (.node(flags_in[1]));
  Pull_Resistor pull_resistor_160 (.node(flags_in[2]));
  Pull_Resistor pull_resistor_161 (.node(flags_in[3]));
  Pull_Resistor pull_resistor_162 (.node(flags_in[4]));
  Transistor transistor_417 (.in(reg1_read_data[8]), .out(reg_write_data[0]), .gate(not_60_out));
  Transistor transistor_418 (.in(reg1_read_data[9]), .out(reg_write_data[1]), .gate(not_60_out));
  Transistor transistor_419 (.in(reg1_read_data[10]), .out(reg_write_data[2]), .gate(not_60_out));
  Transistor transistor_420 (.in(reg1_read_data[11]), .out(reg_write_data[3]), .gate(not_60_out));
  Transistor transistor_421 (.in(reg1_read_data[12]), .out(reg_write_data[4]), .gate(not_60_out));
  Transistor transistor_422 (.in(reg1_read_data[13]), .out(reg_write_data[5]), .gate(not_60_out));
  Transistor transistor_423 (.in(reg1_read_data[14]), .out(reg_write_data[6]), .gate(not_60_out));
  Transistor transistor_424 (.in(reg1_read_data[15]), .out(reg_write_data[7]), .gate(not_60_out));
  Transistor transistor_425 (.in(reg1_read_data[0]), .out(reg_write_data[8]), .gate(not_60_out));
  Transistor transistor_426 (.in(reg1_read_data[1]), .out(reg_write_data[9]), .gate(not_60_out));
  Transistor transistor_427 (.in(reg1_read_data[2]), .out(reg_write_data[10]), .gate(not_60_out));
  Transistor transistor_428 (.in(reg1_read_data[3]), .out(reg_write_data[11]), .gate(not_60_out));
  Transistor transistor_429 (.in(reg1_read_data[4]), .out(reg_write_data[12]), .gate(not_60_out));
  Transistor transistor_430 (.in(reg1_read_data[5]), .out(reg_write_data[13]), .gate(not_60_out));
  Transistor transistor_431 (.in(reg1_read_data[6]), .out(reg_write_data[14]), .gate(not_60_out));
  Transistor transistor_432 (.in(reg1_read_data[7]), .out(reg_write_data[15]), .gate(not_60_out));
  not not_60 (not_60_out, alu_swp);

  // Notes on the sheet:
  //   contents of rom_1 (hex, n*v repeats v):
  //   0 a 20 5 0 0 2 43 41 83 81 3 1 3 1 3 1 0 2 10 12 1 3 1 0 2 0 2 0 2
  //   contents of rom_2 (hex, n*v repeats v):
  //   0 0 0 4 4 4c 48 0 4 0 4 2 6 1 5 10 14 c 8 c 8 c 8 20 c 8 c 8 4c 48
  //   contents of rom_3 (hex, n*v repeats v):
  //   0 1 1 80 1 20 20 8*1 8 8 20 20 1 1 10 10 1 4 4 40 40 40
  //   contents of ROM_1 (hex, n*v repeats v):
  //   2 0 0 0 10 0 0 0 11 0 fc 241*0 2 0 f0 f0 10 0 f0 f0 10 0 f f 13 0 0 80 15 0 1 80 17 0 0 0 3 0 0 0 3
  //   0 0 3 18
endmodule

module test (
);

  wire button_1_out, button_2_out, button_3_out, not_1_out, not_2_out, undriven_2, xor_1_out;
  wire [3:0] transistor_1_out;
  wire [7:0] transistor_9_out, undriven;

  Transistor transistor_1 (.in(1'b1), .out(transistor_1_out[0]), .gate(not_1_out));
  Transistor transistor_2 (.in(1'b0), .out(transistor_1_out[1]), .gate(not_1_out));
  Transistor transistor_3 (.in(1'b1), .out(transistor_1_out[2]), .gate(not_1_out));
  Transistor transistor_4 (.in(1'b0), .out(transistor_1_out[3]), .gate(not_1_out));
  not not_1 (not_1_out, button_1_out);
  Button button_1 (.out(button_1_out));
  Pull_Resistor pull_resistor_1 (.node(transistor_1_out[0]));
  Pull_Resistor pull_resistor_2 (.node(transistor_1_out[1]));
  Pull_Resistor pull_resistor_3 (.node(transistor_1_out[2]));
  Pull_Resistor pull_resistor_4 (.node(transistor_1_out[3]));
  Transistor transistor_5 (.in(1'b1), .out(transistor_1_out[0]), .gate(not_2_out));
  Transistor transistor_6 (.in(1'b0), .out(transistor_1_out[1]), .gate(not_2_out));
  Transistor transistor_7 (.in(1'b1), .out(transistor_1_out[2]), .gate(not_2_out));
  Transistor transistor_8 (.in(1'b0), .out(transistor_1_out[3]), .gate(not_2_out));
  not not_2 (not_2_out, button_2_out);
  Button button_2 (.out(button_2_out));
  Transistor transistor_9 (.in(undriven[0]), .out(transistor_9_out[0]), .gate(undriven_2));
  Transistor transistor_10 (.in(undriven[1]), .out(transistor_9_out[1]), .gate(undriven_2));
  Transistor transistor_11 (.in(undriven[2]), .out(transistor_9_out[2]), .gate(undriven_2));
  Transistor transistor_12 (.in(undriven[3]), .out(transistor_9_out[3]), .gate(undriven_2));
  Transistor transistor_13 (.in(undriven[4]), .out(transistor_9_out[4]), .gate(undriven_2));
  Transistor transistor_14 (.in(undriven[5]), .out(transistor_9_out[5]), .gate(undriven_2));
  Transistor transistor_15 (.in(undriven[6]), .out(transistor_9_out[6]), .gate(undriven_2));
  Transistor transistor_16 (.in(undriven[7]), .out(transistor_9_out[7]), .gate(undriven_2));
  Pull_Resistor pull_resistor_5 (.node(transistor_9_out[0]));
  Pull_Resistor pull_resistor_6 (.node(transistor_9_out[1]));
  Pull_Resistor pull_resistor_7 (.node(transistor_9_out[2]));
  Pull_Resistor pull_resistor_8 (.node(transistor_9_out[3]));
  Pull_Resistor pull_resistor_9 (.node(transistor_9_out[4]));
  Pull_Resistor pull_resistor_10 (.node(transistor_9_out[5]));
  Pull_Resistor pull_resistor_11 (.node(transistor_9_out[6]));
  Pull_Resistor pull_resistor_12 (.node(transistor_9_out[7]));
  Button button_3 (.out(button_3_out));
  xor xor_1 (xor_1_out, button_3_out, 1'b1);
endmodule
